// Logisim project main.circ as structural Verilog: 8 circuits, main circuit main
module main (
  input  Full_On,
  input  Selection_On
);

  wire and_3_out, and_4_out, and_5_out, and_6_out, and_7_out, and_8_out, and_9_out, and_10_out, and_11_out,
       and_12_out, cdm_8_mark5_1_p1, cdm_8_mark5_1_p2, cdm_8_mark5_1_p4, cdm_8_mark5_1_p5, cdm_8_mark5_1_p6,
       cdm_8_mark5_1_p7, cdm_8_mark5_1_p8, cdm_8_mark5_1_p9, clock, code, comparator_1_lt, comparator_2_eq,
       comparator_3_eq, comparator_4_eq, comparator_5_eq, comparator_6_eq, comparator_7_eq, comparator_8_eq,
       comparator_9_eq, comparator_10_eq, comparator_11_eq, data, decoder_3_out0, decoder_4_out1,
       decoder_5_out0, decoder_5_out1, decoder_6_out0, decoder_7_out1, decoder_8_out0, decoder_8_out1,
       decoder_9_out1, decoder_10_out0, decoder_10_out1, decoder_11_out0, decoder_11_out1, in_out, IOsel,
       mem, n32_bit_row_destructor_1_selected_bit, not_1_out, not_2_out, not_3_out, not_4_out, not_5_out,
       not_6_out, not_7_out, not_8_out, not_9_out, or_1_out, or_2_out, or_3_out, or_4_out, RAM, row_read,
       row_write;
  wire [4:0] keyboard_controller_1_x, keyboard_controller_1_y;
  wire [6:0] keyboard_1_data;
  wire [7:0] addr, bus, byte0, byte1, byte2, byte3, cdm_8_mark5_1_p13, cdm_8_mark5_1_p14,
       controlled_buffer_3_out, controlled_buffer_6_out, controlled_buffer_7_out, controlled_buffer_12_out,
       controlled_buffer_17_out, controlled_buffer_21_out, counter_1_q, inc_1_p3, inc_2_p2, inc_3_p2,
       n32_bit_row_destructor_1_selected_byte, register_2_q, register_3_q, register_5_q, register_6_q,
       register_7_q, register_8_q, register_9_q;
  wire [31:0] n32_32_buffer_1_row_0, n32_32_buffer_1_row_1, n32_32_buffer_1_row_2, n32_32_buffer_1_row_3,
       n32_32_buffer_1_row_4, n32_32_buffer_1_row_5, n32_32_buffer_1_row_6, n32_32_buffer_1_row_7,
       n32_32_buffer_1_row_8, n32_32_buffer_1_row_9, n32_32_buffer_1_row_10, n32_32_buffer_1_row_11,
       n32_32_buffer_1_row_12, n32_32_buffer_1_row_13, n32_32_buffer_1_row_14, n32_32_buffer_1_row_15,
       n32_32_buffer_1_row_16, n32_32_buffer_1_row_17, n32_32_buffer_1_row_18, n32_32_buffer_1_row_19,
       n32_32_buffer_1_row_20, n32_32_buffer_1_row_21, n32_32_buffer_1_row_22, n32_32_buffer_1_row_23,
       n32_32_buffer_1_row_24, n32_32_buffer_1_row_25, n32_32_buffer_1_row_26, n32_32_buffer_1_row_27,
       n32_32_buffer_1_row_28, n32_32_buffer_1_row_29, n32_32_buffer_1_row_30, n32_32_buffer_1_row_31,
       n32_32_buffer_1_selected_row_output, random_1_out;

  // Probe on cdm_8_mark5_1_p2
  // Probe on cdm_8_mark5_1_p1
  Clock clock_1 (.out(clock));
  and and_1 (IOsel, not_1_out, clock, data);
  // Probe on cdm_8_mark5_1_p4
  // Probe on cdm_8_mark5_1_p5
  // Probe on cdm_8_mark5_1_p6
  not not_1 (not_1_out, comparator_1_lt);
  // Probe on cdm_8_mark5_1_p7
  // Probe on cdm_8_mark5_1_p8
  // CdM_8_mark5 cdm_8_mark5_1: pin names not known; wires that end beside it: cdm_8_mark5_1_p1, cdm_8_mark5_1_p2, clock, cdm_8_mark5_1_p4, cdm_8_mark5_1_p5, cdm_8_mark5_1_p6, cdm_8_mark5_1_p7, cdm_8_mark5_1_p8, cdm_8_mark5_1_p9, mem, in_out, addr, cdm_8_mark5_1_p13, cdm_8_mark5_1_p14
  assign bus = not_2_out ? cdm_8_mark5_1_p13 : 8'bz;  // Controlled_Buffer controlled_buffer_1
  not not_2 (not_2_out, in_out);
  and and_2 (RAM, comparator_1_lt, data);
  not not_3 (not_3_out, not_3_out);
  Decoder #(.disabled(0)) decoder_1 (.out0(code), .out1(data), .sel(cdm_8_mark5_1_p9), .en(mem));
  assign cdm_8_mark5_1_p14 = in_out ? bus : 8'bz;  // Controlled_Buffer controlled_buffer_2
  not not_4 (not_4_out, not_4_out);
  not not_5 (not_5_out, not_5_out);
  // Probe on addr
  Comparator #(.mode("unsigned")) comparator_1 (.a(addr), .b(8'hf0), .lt(comparator_1_lt));  // open: gt, eq
  assign controlled_buffer_3_out = decoder_3_out0 ? bus : 8'bz;  // Controlled_Buffer controlled_buffer_3
  // Probe on bus
  ROM rom_1 (.addr(addr), .data(bus), .sel(code));
  RAM ram_1 (.addr(addr), .data(bus), .sel(RAM), .clk(clock), .ld(in_out));  // open: clr
  assign bus = row_read ? {8{1'b0}} : 8'bz;  // Controlled_Buffer controlled_buffer_4
  Register register_1 (.D(controlled_buffer_3_out), .clk(decoder_3_out0));  // open: en, Q, clr
  assign bus = decoder_4_out1 ? register_2_q : 8'bz;  // Controlled_Buffer controlled_buffer_5
  Register register_2 (.Q(register_2_q));  // open: D, en, clk, clr
  Comparator comparator_2 (.a(addr), .b(8'hf5), .eq(comparator_2_eq));  // open: gt, lt
  Decoder #(.disabled(0)) decoder_2 (.out0(row_write), .out1(row_read), .sel(in_out), .en(and_3_out));
  Comparator comparator_3 (.a(addr), .b(8'hf3), .eq(comparator_3_eq));  // open: gt, lt
  Decoder #(.disabled(0)) decoder_3 (.out0(decoder_3_out0), .sel(in_out), .en(and_4_out));  // open: out1
  Comparator comparator_4 (.a(addr), .b(8'hf0), .eq(comparator_4_eq));  // open: gt, lt
  Decoder #(.disabled(0)) decoder_4 (.out1(decoder_4_out1), .sel(in_out), .en(and_5_out));  // open: out0
  Keyboard keyboard_1 (.clk(clock), .re(1'b1), .data(keyboard_1_data));  // open: clr, avail
  and and_3 (and_3_out, comparator_2_eq, IOsel);
  and and_4 (and_4_out, comparator_3_eq, IOsel);
  and and_5 (and_5_out, comparator_4_eq, IOsel);
  not not_6 (not_6_out, not_6_out);
  not not_7 (not_7_out, not_7_out);
  Keyboard_controller keyboard_controller_1 (
    .ASCII_code(keyboard_1_data), .X(keyboard_controller_1_x), .Y(keyboard_controller_1_y));
  assign controlled_buffer_6_out = row_read ? byte0 : 8'bz;  // Controlled_Buffer controlled_buffer_6
  assign controlled_buffer_7_out = decoder_6_out0 ? bus : 8'bz;  // Controlled_Buffer controlled_buffer_7
  Random #(.width(32), .seed(10)) random_1 (.clk(clock), .next(Full_On), .out(random_1_out));  // open: clr
  Counter #(.max('h1f)) counter_1 (.count(Full_On), .Q(counter_1_q), .clk(clock));  // open: load, D, carry, clr
  assign controlled_buffer_6_out = decoder_5_out0 ? bus : 8'bz;  // Controlled_Buffer controlled_buffer_8
  assign bus = decoder_5_out1 ? register_3_q : 8'bz;  // Controlled_Buffer controlled_buffer_9
  Register register_3 (.D(controlled_buffer_6_out), .Q(register_3_q), .clk(or_1_out));  // open: en, clr
  or or_1 (or_1_out, row_read, decoder_5_out0);
  Register register_4 (.D(controlled_buffer_7_out), .clk(decoder_6_out0));  // open: en, Q, clr
  assign bus = decoder_7_out1 ? register_5_q : 8'bz;  // Controlled_Buffer controlled_buffer_10
  Register register_5 (.Q(register_5_q));  // open: D, en, clk, clr
  // Probe on keyboard_controller_1_y
  // Probe on keyboard_controller_1_x
  Decoder #(.disabled(0)) decoder_5 (.out0(decoder_5_out0), .out1(decoder_5_out1), .sel(in_out), .en(and_6_out));
  assign byte0 = row_write ? register_3_q : 8'bz;  // Controlled_Buffer controlled_buffer_11
  Decoder #(.disabled(0)) decoder_6 (.out0(decoder_6_out0), .sel(in_out), .en(and_7_out));  // open: out1
  Decoder #(.disabled(0)) decoder_7 (.out1(decoder_7_out1), .sel(in_out), .en(and_8_out));  // open: out0
  _32_32_buffer u_32_32_buffer_1 (
    .Row_0(n32_32_buffer_1_row_0), .Row_1(n32_32_buffer_1_row_1), .Row_2(n32_32_buffer_1_row_2),
    .Row_3(n32_32_buffer_1_row_3), .Row_4(n32_32_buffer_1_row_4), .Row_5(n32_32_buffer_1_row_5),
    .Row_6(n32_32_buffer_1_row_6), .Row_7(n32_32_buffer_1_row_7), .Row_8(n32_32_buffer_1_row_8),
    .Row_9(n32_32_buffer_1_row_9), .Row_10(n32_32_buffer_1_row_10), .Row_11(n32_32_buffer_1_row_11),
    .Row_12(n32_32_buffer_1_row_12), .Row_13(n32_32_buffer_1_row_13), .Row_14(n32_32_buffer_1_row_14),
    .Row_15(n32_32_buffer_1_row_15), .Row_16(n32_32_buffer_1_row_16), .Row_17(n32_32_buffer_1_row_17),
    .Row_18(n32_32_buffer_1_row_18), .Row_19(n32_32_buffer_1_row_19), .Row_20(n32_32_buffer_1_row_20),
    .Row_21(n32_32_buffer_1_row_21), .Row_22(n32_32_buffer_1_row_22), .Row_23(n32_32_buffer_1_row_23),
    .Row_24(n32_32_buffer_1_row_24), .Row_25(n32_32_buffer_1_row_25), .Row_26(n32_32_buffer_1_row_26),
    .Row_27(n32_32_buffer_1_row_27), .Row_28(n32_32_buffer_1_row_28), .Row_29(n32_32_buffer_1_row_29),
    .Row_30(n32_32_buffer_1_row_30), .Row_31(n32_32_buffer_1_row_31), .Row_selector(counter_1_q),
    .Write_row(Selection_On), .Input_row(random_1_out), .clock(clock),
    .Output_row_selector(keyboard_controller_1_y), .Selected_row_output(n32_32_buffer_1_selected_row_output));
  Comparator comparator_5 (.a(addr), .b(8'hf6), .eq(comparator_5_eq));  // open: gt, lt
  and and_6 (and_6_out, comparator_5_eq, IOsel);
  Comparator comparator_6 (.a(addr), .b(8'hf4), .eq(comparator_6_eq));  // open: gt, lt
  and and_7 (and_7_out, comparator_6_eq, IOsel);
  Comparator comparator_7 (.a(addr), .b(8'hf1), .eq(comparator_7_eq));  // open: gt, lt
  and and_8 (and_8_out, comparator_7_eq, IOsel);
  _32_bit_row_destructor u_32_bit_row_destructor_1 (
    .Row(n32_32_buffer_1_selected_row_output), .Bit_selector(keyboard_controller_1_x),
    .Selected_byte(n32_bit_row_destructor_1_selected_byte),
    .Selected_bit(n32_bit_row_destructor_1_selected_bit));
  DotMatrix #(.inputtype("row"), .matrixcols(32), .matrixrows(32)) dotmatrix_1 (
    .row0(n32_32_buffer_1_row_0), .row1(n32_32_buffer_1_row_1), .row2(n32_32_buffer_1_row_2),
    .row3(n32_32_buffer_1_row_3), .row4(n32_32_buffer_1_row_4), .row5(n32_32_buffer_1_row_5),
    .row6(n32_32_buffer_1_row_6), .row7(n32_32_buffer_1_row_7), .row8(n32_32_buffer_1_row_8),
    .row9(n32_32_buffer_1_row_9), .row10(n32_32_buffer_1_row_10), .row11(n32_32_buffer_1_row_11),
    .row12(n32_32_buffer_1_row_12), .row13(n32_32_buffer_1_row_13), .row14(n32_32_buffer_1_row_14),
    .row15(n32_32_buffer_1_row_15), .row16(n32_32_buffer_1_row_16), .row17(n32_32_buffer_1_row_17),
    .row18(n32_32_buffer_1_row_18), .row19(n32_32_buffer_1_row_19), .row20(n32_32_buffer_1_row_20),
    .row21(n32_32_buffer_1_row_21), .row22(n32_32_buffer_1_row_22), .row23(n32_32_buffer_1_row_23),
    .row24(n32_32_buffer_1_row_24), .row25(n32_32_buffer_1_row_25), .row26(n32_32_buffer_1_row_26),
    .row27(n32_32_buffer_1_row_27), .row28(n32_32_buffer_1_row_28), .row29(n32_32_buffer_1_row_29),
    .row30(n32_32_buffer_1_row_30), .row31(n32_32_buffer_1_row_31));
  // inc inc_1: pin names not known; wires that end beside it: addr, 8'hf6, inc_1_p3
  assign controlled_buffer_12_out = row_read ? byte1 : 8'bz;  // Controlled_Buffer controlled_buffer_12
  not not_8 (not_8_out, not_8_out);
  // Probe on n32_32_buffer_1_selected_row_output
  // Probe on n32_bit_row_destructor_1_selected_byte
  // Probe on n32_bit_row_destructor_1_selected_bit
  assign controlled_buffer_12_out = decoder_8_out0 ? bus : 8'bz;  // Controlled_Buffer controlled_buffer_13
  assign bus = decoder_8_out1 ? register_6_q : 8'bz;  // Controlled_Buffer controlled_buffer_14
  Register register_6 (.D(controlled_buffer_12_out), .Q(register_6_q), .clk(or_2_out));  // open: en, clr
  or or_2 (or_2_out, row_read, decoder_8_out0);
  // Probe on inc_1_p3
  Decoder #(.disabled(0)) decoder_8 (.out0(decoder_8_out0), .out1(decoder_8_out1), .sel(in_out), .en(and_9_out));
  assign byte1 = row_write ? register_6_q : 8'bz;  // Controlled_Buffer controlled_buffer_15
  Comparator comparator_8 (.a(addr), .b(inc_1_p3), .eq(comparator_8_eq));  // open: gt, lt
  and and_9 (and_9_out, comparator_8_eq, IOsel);
  assign bus = decoder_9_out1 ? register_7_q : 8'bz;  // Controlled_Buffer controlled_buffer_16
  Register register_7 (.Q(register_7_q));  // open: D, en, clk, clr
  Comparator comparator_9 (.a(addr), .b(8'hf2), .eq(comparator_9_eq));  // open: gt, lt
  Decoder #(.disabled(0)) decoder_9 (.out1(decoder_9_out1), .sel(in_out), .en(and_10_out));  // open: out0
  // inc inc_2: pin names not known; wires that end beside it: inc_1_p3, inc_2_p2
  assign controlled_buffer_17_out = decoder_10_out0 ? bus : 8'bz;  // Controlled_Buffer controlled_buffer_17
  assign controlled_buffer_17_out = row_read ? byte2 : 8'bz;  // Controlled_Buffer controlled_buffer_18
  and and_10 (and_10_out, comparator_9_eq, IOsel);
  assign bus = decoder_10_out1 ? register_8_q : 8'bz;  // Controlled_Buffer controlled_buffer_19
  Register register_8 (.D(controlled_buffer_17_out), .Q(register_8_q), .clk(or_3_out));  // open: en, clr
  or or_3 (or_3_out, row_read, decoder_10_out0);
  // Probe on inc_2_p2
  Decoder #(.disabled(0)) decoder_10 (.out0(decoder_10_out0), .out1(decoder_10_out1), .sel(in_out), .en(and_11_out));
  assign byte2 = row_write ? register_8_q : 8'bz;  // Controlled_Buffer controlled_buffer_20
  Comparator comparator_10 (.a(addr), .b(inc_2_p2), .eq(comparator_10_eq));  // open: gt, lt
  and and_11 (and_11_out, comparator_10_eq, IOsel);
  // inc inc_3: pin names not known; wires that end beside it: inc_2_p2, inc_3_p2
  assign controlled_buffer_21_out = decoder_11_out0 ? bus : 8'bz;  // Controlled_Buffer controlled_buffer_21
  assign controlled_buffer_21_out = row_read ? byte3 : 8'bz;  // Controlled_Buffer controlled_buffer_22
  assign bus = decoder_11_out1 ? register_9_q : 8'bz;  // Controlled_Buffer controlled_buffer_23
  Register register_9 (.D(controlled_buffer_21_out), .Q(register_9_q), .clk(or_4_out));  // open: en, clr
  or or_4 (or_4_out, row_read, decoder_11_out0);
  // Probe on inc_3_p2
  Decoder #(.disabled(0)) decoder_11 (.out0(decoder_11_out0), .out1(decoder_11_out1), .sel(in_out), .en(and_12_out));
  assign byte3 = row_write ? register_9_q : 8'bz;  // Controlled_Buffer controlled_buffer_24
  Comparator comparator_11 (.a(addr), .b(inc_3_p2), .eq(comparator_11_eq));  // open: gt, lt
  and and_12 (and_12_out, comparator_11_eq, IOsel);
  not not_9 (not_9_out, not_9_out);

  // Other names for the same wires on the sheet: IOaddr[7:0] = addr; IOdata[7:0] = bus; on = Full_On; rd_wr = in_out

  // Notes on the sheet:
  //   ROW READ / WRITE
  //   PROCESSED CELL
  //   (read only thus CdM -> buffer)
  //   READ ONLY INPUTS
  //   (immutable game state)
  //   Structure of I/O bus
  //   Harvard Architecture
  //   Minimal IO cell address
  //   Cell 0xf5 (row data direction)
  //   Cell 0xf3 (Y - row)
  //   Cell 0xf0 (state)
  //   contents of rom_1 (hex, n*v repeats v):
  //   cc f0 d0 f0 a e1 a b2 ee 4 2a a2 d4
  //   Keyboard
  //   Cells 0xf6-0xf9
  //   (little endtiand row's bytes)
  //   Cell 0xf4 (X - bit)
  //   Cell 0xf1 (birth conditions)
  //   Cell 0xf2 (survival conditions)
endmodule

module _16_16_matrix (
  input  [7:0] Lo_byte,
  input  Lo_byte_on,
  input  [7:0] Hi_byte,
  input  Hi_byte_On,
  input  [7:0] Selector,
  input  Selection_On,
  input  Bus_0
);

  wire clk, demultiplexer_1_out0, demultiplexer_1_out1, demultiplexer_1_out2, demultiplexer_1_out3,
       demultiplexer_1_out4, demultiplexer_1_out5, demultiplexer_1_out6, demultiplexer_1_out7,
       demultiplexer_1_out8, demultiplexer_1_out9, demultiplexer_1_out10, demultiplexer_1_out11,
       demultiplexer_1_out12, demultiplexer_1_out13, demultiplexer_1_out14, demultiplexer_1_out15;
  wire [7:0] register_1_q, register_2_q, register_3_q;
  wire [15:0] register_4_q, register_5_q, register_6_q, register_7_q, register_8_q, register_9_q,
       register_10_q, register_11_q, register_12_q, register_13_q, register_14_q, register_15_q,
       register_16_q, register_17_q, register_18_q, register_19_q;

  Clock clock_1 (.out(clk));
  Register register_1 (.D(Lo_byte), .en(Lo_byte_on), .Q(register_1_q), .clk(clk));  // open: clr
  Register register_2 (.D(Hi_byte), .en(Hi_byte_On), .Q(register_2_q), .clk(clk));  // open: clr
  Register #(.trigger("high")) register_3 (.D(Selector), .en(Selection_On), .Q(register_3_q), .clk(clk));  // open: clr
  // Probe on register_3_q
  Demultiplexer #(.select(4), .disabled(0)) demultiplexer_1 (
    .out0(demultiplexer_1_out0), .out1(demultiplexer_1_out1), .out2(demultiplexer_1_out2),
    .out3(demultiplexer_1_out3), .out4(demultiplexer_1_out4), .out5(demultiplexer_1_out5),
    .out6(demultiplexer_1_out6), .out7(demultiplexer_1_out7), .out8(demultiplexer_1_out8),
    .out9(demultiplexer_1_out9), .out10(demultiplexer_1_out10), .out11(demultiplexer_1_out11),
    .out12(demultiplexer_1_out12), .out13(demultiplexer_1_out13), .out14(demultiplexer_1_out14),
    .out15(demultiplexer_1_out15), .in(Selection_On), .sel(register_3_q[3:0]), .en(Selection_On));
  Register #(.width(16)) register_4 (
    .D({register_2_q, register_1_q}), .en(demultiplexer_1_out0), .Q(register_4_q), .clk(clk));  // open: clr
  Register #(.width(16)) register_5 (
    .D({register_2_q, register_1_q}), .en(demultiplexer_1_out1), .Q(register_5_q), .clk(clk));  // open: clr
  Register #(.width(16)) register_6 (
    .D({register_2_q, register_1_q}), .en(demultiplexer_1_out2), .Q(register_6_q), .clk(clk));  // open: clr
  Register #(.width(16)) register_7 (
    .D({register_2_q, register_1_q}), .en(demultiplexer_1_out3), .Q(register_7_q), .clk(clk));  // open: clr
  Register #(.width(16)) register_8 (
    .D({register_2_q, register_1_q}), .en(demultiplexer_1_out4), .Q(register_8_q), .clk(clk));  // open: clr
  Register #(.width(16)) register_9 (
    .D({register_2_q, register_1_q}), .en(demultiplexer_1_out5), .Q(register_9_q), .clk(clk));  // open: clr
  Register #(.width(16)) register_10 (
    .D({register_2_q, register_1_q}), .en(demultiplexer_1_out6), .Q(register_10_q), .clk(clk));  // open: clr
  Register #(.width(16)) register_11 (
    .D({register_2_q, register_1_q}), .en(demultiplexer_1_out7), .Q(register_11_q), .clk(clk));  // open: clr
  Register #(.width(16)) register_12 (
    .D({register_2_q, register_1_q}), .en(demultiplexer_1_out8), .Q(register_12_q), .clk(clk));  // open: clr
  Register #(.width(16)) register_13 (
    .D({register_2_q, register_1_q}), .en(demultiplexer_1_out9), .Q(register_13_q), .clk(clk));  // open: clr
  Register #(.width(16)) register_14 (
    .D({register_2_q, register_1_q}), .en(demultiplexer_1_out10), .Q(register_14_q), .clk(clk));  // open: clr
  Register #(.width(16)) register_15 (
    .D({register_2_q, register_1_q}), .en(demultiplexer_1_out11), .Q(register_15_q), .clk(clk));  // open: clr
  Register #(.width(16)) register_16 (
    .D({register_2_q, register_1_q}), .en(demultiplexer_1_out12), .Q(register_16_q), .clk(clk));  // open: clr
  Register #(.width(16)) register_17 (
    .D({register_2_q, register_1_q}), .en(demultiplexer_1_out13), .Q(register_17_q), .clk(clk));  // open: clr
  Register #(.width(16)) register_18 (
    .D({register_2_q, register_1_q}), .en(demultiplexer_1_out14), .Q(register_18_q), .clk(clk));  // open: clr
  Register #(.width(16)) register_19 (
    .D({register_2_q, register_1_q}), .en(demultiplexer_1_out15), .Q(register_19_q), .clk(clk));  // open: clr
  DotMatrix #(.inputtype("row"), .matrixcols(16), .matrixrows(16)) dotmatrix_1 (
    .row0(register_4_q), .row1(register_5_q), .row2(register_6_q), .row3(register_7_q), .row4(register_8_q),
    .row5(register_9_q), .row6(register_10_q), .row7(register_11_q), .row8(register_12_q),
    .row9(register_13_q), .row10(register_14_q), .row11(register_15_q), .row12(register_16_q),
    .row13(register_17_q), .row14(register_18_q), .row15(register_19_q));
endmodule

module _16_16_demonstration (
  input  Full_On,
  input  Selection_On,
  input  Bus_0
);

  wire clk, demultiplexer_1_out0, demultiplexer_1_out1, demultiplexer_1_out2, demultiplexer_1_out3,
       demultiplexer_1_out4, demultiplexer_1_out5, demultiplexer_1_out6, demultiplexer_1_out7,
       demultiplexer_1_out8, demultiplexer_1_out9, demultiplexer_1_out10, demultiplexer_1_out11,
       demultiplexer_1_out12, demultiplexer_1_out13, demultiplexer_1_out14, demultiplexer_1_out15, rst;
  wire [3:0] random_1_out;
  wire [15:0] random_2_out, register_1_q, register_2_q, register_3_q, register_4_q, register_5_q,
       register_6_q, register_7_q, register_8_q, register_9_q, register_10_q, register_11_q, register_12_q,
       register_13_q, register_14_q, register_15_q, register_16_q;

  Clock clock_1 (.out(clk));
  Button Reset (.out(rst));
  Demultiplexer #(.select(4), .disabled(0)) demultiplexer_1 (
    .out0(demultiplexer_1_out0), .out1(demultiplexer_1_out1), .out2(demultiplexer_1_out2),
    .out3(demultiplexer_1_out3), .out4(demultiplexer_1_out4), .out5(demultiplexer_1_out5),
    .out6(demultiplexer_1_out6), .out7(demultiplexer_1_out7), .out8(demultiplexer_1_out8),
    .out9(demultiplexer_1_out9), .out10(demultiplexer_1_out10), .out11(demultiplexer_1_out11),
    .out12(demultiplexer_1_out12), .out13(demultiplexer_1_out13), .out14(demultiplexer_1_out14),
    .out15(demultiplexer_1_out15), .in(Selection_On), .sel(random_1_out), .en(Selection_On));
  Random #(.width(4)) random_1 (.clk(clk), .next(Full_On), .out(random_1_out), .clr(rst));
  Random #(.width(16), .seed(5)) random_2 (.clk(clk), .next(Full_On), .out(random_2_out), .clr(rst));
  Register #(.width(16)) register_1 (
    .D(random_2_out), .en(demultiplexer_1_out0), .Q(register_1_q), .clk(clk), .clr(rst));
  Register #(.width(16)) register_2 (
    .D(random_2_out), .en(demultiplexer_1_out1), .Q(register_2_q), .clk(clk), .clr(rst));
  Register #(.width(16)) register_3 (
    .D(random_2_out), .en(demultiplexer_1_out2), .Q(register_3_q), .clk(clk), .clr(rst));
  Register #(.width(16)) register_4 (
    .D(random_2_out), .en(demultiplexer_1_out3), .Q(register_4_q), .clk(clk), .clr(rst));
  Register #(.width(16)) register_5 (
    .D(random_2_out), .en(demultiplexer_1_out4), .Q(register_5_q), .clk(clk), .clr(rst));
  Register #(.width(16)) register_6 (
    .D(random_2_out), .en(demultiplexer_1_out5), .Q(register_6_q), .clk(clk), .clr(rst));
  Register #(.width(16)) register_7 (
    .D(random_2_out), .en(demultiplexer_1_out6), .Q(register_7_q), .clk(clk), .clr(rst));
  Register #(.width(16)) register_8 (
    .D(random_2_out), .en(demultiplexer_1_out7), .Q(register_8_q), .clk(clk), .clr(rst));
  Register #(.width(16)) register_9 (
    .D(random_2_out), .en(demultiplexer_1_out8), .Q(register_9_q), .clk(clk), .clr(rst));
  Register #(.width(16)) register_10 (
    .D(random_2_out), .en(demultiplexer_1_out9), .Q(register_10_q), .clk(clk), .clr(rst));
  Register #(.width(16)) register_11 (
    .D(random_2_out), .en(demultiplexer_1_out10), .Q(register_11_q), .clk(clk), .clr(rst));
  Register #(.width(16)) register_12 (
    .D(random_2_out), .en(demultiplexer_1_out11), .Q(register_12_q), .clk(clk), .clr(rst));
  Register #(.width(16)) register_13 (
    .D(random_2_out), .en(demultiplexer_1_out12), .Q(register_13_q), .clk(clk), .clr(rst));
  Register #(.width(16)) register_14 (
    .D(random_2_out), .en(demultiplexer_1_out13), .Q(register_14_q), .clk(clk), .clr(rst));
  Register #(.width(16)) register_15 (
    .D(random_2_out), .en(demultiplexer_1_out14), .Q(register_15_q), .clk(clk), .clr(rst));
  Register #(.width(16)) register_16 (
    .D(random_2_out), .en(demultiplexer_1_out15), .Q(register_16_q), .clk(clk), .clr(rst));
  DotMatrix #(.inputtype("row"), .matrixcols(16), .matrixrows(16)) dotmatrix_1 (
    .row0(register_1_q), .row1(register_2_q), .row2(register_3_q), .row3(register_4_q), .row4(register_5_q),
    .row5(register_6_q), .row6(register_7_q), .row7(register_8_q), .row8(register_9_q), .row9(register_10_q),
    .row10(register_11_q), .row11(register_12_q), .row12(register_13_q), .row13(register_14_q),
    .row14(register_15_q), .row15(register_16_q));

  // Other names for the same wires on the sheet: on = Full_On
endmodule

module _32_32_matrix (
  input  [7:0] _0_byte,
  input  _0_byte_on,
  input  [7:0] _1_byte,
  input  _1_byte_On,
  input  [7:0] _2_byte,
  input  _2_byte_on,
  input  [7:0] _3_byte,
  input  _3_byte_On,
  input  [7:0] Selector,
  input  Selection_On,
  input  Bus_0
);

  wire clk, demultiplexer_1_out0, demultiplexer_1_out1, demultiplexer_1_out2, demultiplexer_1_out3,
       demultiplexer_1_out4, demultiplexer_1_out5, demultiplexer_1_out6, demultiplexer_1_out7,
       demultiplexer_1_out8, demultiplexer_1_out9, demultiplexer_1_out10, demultiplexer_1_out11,
       demultiplexer_1_out12, demultiplexer_1_out13, demultiplexer_1_out14, demultiplexer_1_out15,
       demultiplexer_1_out16, demultiplexer_1_out17, demultiplexer_1_out18, demultiplexer_1_out19,
       demultiplexer_1_out20, demultiplexer_1_out21, demultiplexer_1_out22, demultiplexer_1_out23,
       demultiplexer_1_out24, demultiplexer_1_out25, demultiplexer_1_out26, demultiplexer_1_out27,
       demultiplexer_1_out28, demultiplexer_1_out29, demultiplexer_1_out30, demultiplexer_1_out31;
  wire [7:0] register_1_q, register_2_q, register_3_q, register_4_q, register_5_q;
  wire [31:0] register_6_q, register_7_q, register_8_q, register_9_q, register_10_q, register_11_q,
       register_12_q, register_13_q, register_14_q, register_15_q, register_16_q, register_17_q,
       register_18_q, register_19_q, register_20_q, register_21_q, register_22_q, register_23_q,
       register_24_q, register_25_q, register_26_q, register_27_q, register_28_q, register_29_q,
       register_30_q, register_31_q, register_32_q, register_33_q, register_34_q, register_35_q,
       register_36_q, register_37_q;

  Clock clock_1 (.out(clk));
  Register register_1 (.D(_0_byte), .en(_0_byte_on), .Q(register_1_q), .clk(clk));  // open: clr
  Register register_2 (.D(_1_byte), .en(_1_byte_On), .Q(register_2_q), .clk(clk));  // open: clr
  Register register_3 (.D(_2_byte), .en(_2_byte_on), .Q(register_3_q), .clk(clk));  // open: clr
  Register register_4 (.D(_3_byte), .en(_3_byte_On), .Q(register_4_q), .clk(clk));  // open: clr
  Register #(.trigger("high")) register_5 (.D(Selector), .en(Selection_On), .Q(register_5_q), .clk(clk));  // open: clr
  // Probe on register_5_q
  Demultiplexer #(.select(5), .disabled(0)) demultiplexer_1 (
    .out0(demultiplexer_1_out0), .out1(demultiplexer_1_out1), .out2(demultiplexer_1_out2),
    .out3(demultiplexer_1_out3), .out4(demultiplexer_1_out4), .out5(demultiplexer_1_out5),
    .out6(demultiplexer_1_out6), .out7(demultiplexer_1_out7), .out8(demultiplexer_1_out8),
    .out9(demultiplexer_1_out9), .out10(demultiplexer_1_out10), .out11(demultiplexer_1_out11),
    .out12(demultiplexer_1_out12), .out13(demultiplexer_1_out13), .out14(demultiplexer_1_out14),
    .out15(demultiplexer_1_out15), .out16(demultiplexer_1_out16), .out17(demultiplexer_1_out17),
    .out18(demultiplexer_1_out18), .out19(demultiplexer_1_out19), .out20(demultiplexer_1_out20),
    .out21(demultiplexer_1_out21), .out22(demultiplexer_1_out22), .out23(demultiplexer_1_out23),
    .out24(demultiplexer_1_out24), .out25(demultiplexer_1_out25), .out26(demultiplexer_1_out26),
    .out27(demultiplexer_1_out27), .out28(demultiplexer_1_out28), .out29(demultiplexer_1_out29),
    .out30(demultiplexer_1_out30), .out31(demultiplexer_1_out31), .in(Selection_On), .sel(register_5_q[4:0]));  // open: en
  Register #(.width(32)) register_6 (
    .D({register_4_q, register_3_q, register_2_q, register_1_q}), .en(demultiplexer_1_out0),
    .Q(register_6_q), .clk(clk));  // open: clr
  Register #(.width(32)) register_7 (
    .D({register_4_q, register_3_q, register_2_q, register_1_q}), .en(demultiplexer_1_out1),
    .Q(register_7_q), .clk(clk));  // open: clr
  Register #(.width(32)) register_8 (
    .D({register_4_q, register_3_q, register_2_q, register_1_q}), .en(demultiplexer_1_out2),
    .Q(register_8_q), .clk(clk));  // open: clr
  Register #(.width(32)) register_9 (
    .D({register_4_q, register_3_q, register_2_q, register_1_q}), .en(demultiplexer_1_out3),
    .Q(register_9_q), .clk(clk));  // open: clr
  Register #(.width(32)) register_10 (
    .D({register_4_q, register_3_q, register_2_q, register_1_q}), .en(demultiplexer_1_out4),
    .Q(register_10_q), .clk(clk));  // open: clr
  Register #(.width(32)) register_11 (
    .D({register_4_q, register_3_q, register_2_q, register_1_q}), .en(demultiplexer_1_out5),
    .Q(register_11_q), .clk(clk));  // open: clr
  Register #(.width(32)) register_12 (
    .D({register_4_q, register_3_q, register_2_q, register_1_q}), .en(demultiplexer_1_out6),
    .Q(register_12_q), .clk(clk));  // open: clr
  Register #(.width(32)) register_13 (
    .D({register_4_q, register_3_q, register_2_q, register_1_q}), .en(demultiplexer_1_out7),
    .Q(register_13_q), .clk(clk));  // open: clr
  Register #(.width(32)) register_14 (
    .D({register_4_q, register_3_q, register_2_q, register_1_q}), .en(demultiplexer_1_out8),
    .Q(register_14_q), .clk(clk));  // open: clr
  Register #(.width(32)) register_15 (
    .D({register_4_q, register_3_q, register_2_q, register_1_q}), .en(demultiplexer_1_out9),
    .Q(register_15_q), .clk(clk));  // open: clr
  Register #(.width(32)) register_16 (
    .D({register_4_q, register_3_q, register_2_q, register_1_q}), .en(demultiplexer_1_out10),
    .Q(register_16_q), .clk(clk));  // open: clr
  Register #(.width(32)) register_17 (
    .D({register_4_q, register_3_q, register_2_q, register_1_q}), .en(demultiplexer_1_out11),
    .Q(register_17_q), .clk(clk));  // open: clr
  Register #(.width(32)) register_18 (
    .D({register_4_q, register_3_q, register_2_q, register_1_q}), .en(demultiplexer_1_out12),
    .Q(register_18_q), .clk(clk));  // open: clr
  Register #(.width(32)) register_19 (
    .D({register_4_q, register_3_q, register_2_q, register_1_q}), .en(demultiplexer_1_out13),
    .Q(register_19_q), .clk(clk));  // open: clr
  Register #(.width(32)) register_20 (
    .D({register_4_q, register_3_q, register_2_q, register_1_q}), .en(demultiplexer_1_out14),
    .Q(register_20_q), .clk(clk));  // open: clr
  Register #(.width(32)) register_21 (
    .D({register_4_q, register_3_q, register_2_q, register_1_q}), .en(demultiplexer_1_out15),
    .Q(register_21_q), .clk(clk));  // open: clr
  Register #(.width(32)) register_22 (
    .D({register_4_q, register_3_q, register_2_q, register_1_q}), .en(demultiplexer_1_out16),
    .Q(register_22_q), .clk(clk));  // open: clr
  Register #(.width(32)) register_23 (
    .D({register_4_q, register_3_q, register_2_q, register_1_q}), .en(demultiplexer_1_out17),
    .Q(register_23_q), .clk(clk));  // open: clr
  Register #(.width(32)) register_24 (
    .D({register_4_q, register_3_q, register_2_q, register_1_q}), .en(demultiplexer_1_out18),
    .Q(register_24_q), .clk(clk));  // open: clr
  Register #(.width(32)) register_25 (
    .D({register_4_q, register_3_q, register_2_q, register_1_q}), .en(demultiplexer_1_out19),
    .Q(register_25_q), .clk(clk));  // open: clr
  Register #(.width(32)) register_26 (
    .D({register_4_q, register_3_q, register_2_q, register_1_q}), .en(demultiplexer_1_out20),
    .Q(register_26_q), .clk(clk));  // open: clr
  Register #(.width(32)) register_27 (
    .D({register_4_q, register_3_q, register_2_q, register_1_q}), .en(demultiplexer_1_out21),
    .Q(register_27_q), .clk(clk));  // open: clr
  Register #(.width(32)) register_28 (
    .D({register_4_q, register_3_q, register_2_q, register_1_q}), .en(demultiplexer_1_out22),
    .Q(register_28_q), .clk(clk));  // open: clr
  Register #(.width(32)) register_29 (
    .D({register_4_q, register_3_q, register_2_q, register_1_q}), .en(demultiplexer_1_out23),
    .Q(register_29_q), .clk(clk));  // open: clr
  Register #(.width(32)) register_30 (
    .D({register_4_q, register_3_q, register_2_q, register_1_q}), .en(demultiplexer_1_out24),
    .Q(register_30_q), .clk(clk));  // open: clr
  Register #(.width(32)) register_31 (
    .D({register_4_q, register_3_q, register_2_q, register_1_q}), .en(demultiplexer_1_out25),
    .Q(register_31_q), .clk(clk));  // open: clr
  Register #(.width(32)) register_32 (
    .D({register_4_q, register_3_q, register_2_q, register_1_q}), .en(demultiplexer_1_out26),
    .Q(register_32_q), .clk(clk));  // open: clr
  Register #(.width(32)) register_33 (
    .D({register_4_q, register_3_q, register_2_q, register_1_q}), .en(demultiplexer_1_out27),
    .Q(register_33_q), .clk(clk));  // open: clr
  Register #(.width(32)) register_34 (
    .D({register_4_q, register_3_q, register_2_q, register_1_q}), .en(demultiplexer_1_out28),
    .Q(register_34_q), .clk(clk));  // open: clr
  Register #(.width(32)) register_35 (
    .D({register_4_q, register_3_q, register_2_q, register_1_q}), .en(demultiplexer_1_out29),
    .Q(register_35_q), .clk(clk));  // open: clr
  Register #(.width(32)) register_36 (
    .D({register_4_q, register_3_q, register_2_q, register_1_q}), .en(demultiplexer_1_out30),
    .Q(register_36_q), .clk(clk));  // open: clr
  Register #(.width(32)) register_37 (
    .D({register_4_q, register_3_q, register_2_q, register_1_q}), .en(demultiplexer_1_out31),
    .Q(register_37_q), .clk(clk));  // open: clr
  DotMatrix #(.inputtype("row"), .matrixcols(32), .matrixrows(32)) dotmatrix_1 (
    .row0(register_6_q), .row1(register_7_q), .row2(register_8_q), .row3(register_9_q), .row4(register_10_q),
    .row5(register_11_q), .row6(register_12_q), .row7(register_13_q), .row8(register_14_q),
    .row9(register_15_q), .row10(register_16_q), .row11(register_17_q), .row12(register_18_q),
    .row13(register_19_q), .row14(register_20_q), .row15(register_21_q), .row16(register_22_q),
    .row17(register_23_q), .row18(register_24_q), .row19(register_25_q), .row20(register_26_q),
    .row21(register_27_q), .row22(register_28_q), .row23(register_29_q), .row24(register_30_q),
    .row25(register_31_q), .row26(register_32_q), .row27(register_33_q), .row28(register_34_q),
    .row29(register_35_q), .row30(register_36_q), .row31(register_37_q));
endmodule

module _32_32_demo (
  input  Full_On,
  input  Selection_On,
  input  [4:0] Y,
  input  [4:0] X,
  output [31:0] out_5,
  output [7:0] out_6,
  output out_7
);

  wire clk;
  wire [7:0] counter_1_q;
  wire [31:0] n32_32_buffer_1_p7, n32_32_buffer_1_p8, n32_32_buffer_1_p9, n32_32_buffer_1_p10,
       n32_32_buffer_1_p11, n32_32_buffer_1_p12, n32_32_buffer_1_p13, n32_32_buffer_1_p14,
       n32_32_buffer_1_p15, n32_32_buffer_1_p16, n32_32_buffer_1_p17, n32_32_buffer_1_p18,
       n32_32_buffer_1_p19, n32_32_buffer_1_p20, n32_32_buffer_1_p21, n32_32_buffer_1_p22,
       n32_32_buffer_1_p23, n32_32_buffer_1_p24, n32_32_buffer_1_p25, n32_32_buffer_1_p26,
       n32_32_buffer_1_p27, n32_32_buffer_1_p28, n32_32_buffer_1_p29, n32_32_buffer_1_p30,
       n32_32_buffer_1_p31, n32_32_buffer_1_p32, n32_32_buffer_1_p33, n32_32_buffer_1_p34,
       n32_32_buffer_1_p35, n32_32_buffer_1_p36, n32_32_buffer_1_p37, n32_32_buffer_1_p38, random_1_out;

  Clock clock_1 (.out(clk));
  Random #(.width(32), .seed(10)) random_1 (.clk(clk), .next(Full_On), .out(random_1_out));  // open: clr
  Counter #(.max('h1f)) counter_1 (.count(Full_On), .Q(counter_1_q), .clk(clk));  // open: load, D, carry, clr
  // _32_32_buffer 32_32_buffer_1: pin names not known; wires that end beside it: clk, random_1_out, counter_1_q, Selection_On, Y, X, n32_32_buffer_1_p7, n32_32_buffer_1_p8, n32_32_buffer_1_p9, n32_32_buffer_1_p10, n32_32_buffer_1_p11, n32_32_buffer_1_p12, n32_32_buffer_1_p13, n32_32_buffer_1_p14, n32_32_buffer_1_p15, n32_32_buffer_1_p16, n32_32_buffer_1_p17, n32_32_buffer_1_p18, n32_32_buffer_1_p19, n32_32_buffer_1_p20, n32_32_buffer_1_p21, n32_32_buffer_1_p22, n32_32_buffer_1_p23, n32_32_buffer_1_p24, n32_32_buffer_1_p25, n32_32_buffer_1_p26, n32_32_buffer_1_p27, n32_32_buffer_1_p28, n32_32_buffer_1_p29, n32_32_buffer_1_p30, n32_32_buffer_1_p31, n32_32_buffer_1_p32, n32_32_buffer_1_p33, n32_32_buffer_1_p34, n32_32_buffer_1_p35, n32_32_buffer_1_p36, n32_32_buffer_1_p37, n32_32_buffer_1_p38, out_5, out_6, out_7
  // Probe on Y
  // Probe on X
  DotMatrix #(.inputtype("row"), .matrixcols(32), .matrixrows(32)) dotmatrix_1 (
    .row0(n32_32_buffer_1_p7), .row1(n32_32_buffer_1_p8), .row2(n32_32_buffer_1_p9),
    .row3(n32_32_buffer_1_p10), .row4(n32_32_buffer_1_p11), .row5(n32_32_buffer_1_p12),
    .row6(n32_32_buffer_1_p13), .row7(n32_32_buffer_1_p14), .row8(n32_32_buffer_1_p15),
    .row9(n32_32_buffer_1_p16), .row10(n32_32_buffer_1_p17), .row11(n32_32_buffer_1_p18),
    .row12(n32_32_buffer_1_p19), .row13(n32_32_buffer_1_p20), .row14(n32_32_buffer_1_p21),
    .row15(n32_32_buffer_1_p22), .row16(n32_32_buffer_1_p23), .row17(n32_32_buffer_1_p24),
    .row18(n32_32_buffer_1_p25), .row19(n32_32_buffer_1_p26), .row20(n32_32_buffer_1_p27),
    .row21(n32_32_buffer_1_p28), .row22(n32_32_buffer_1_p29), .row23(n32_32_buffer_1_p30),
    .row24(n32_32_buffer_1_p31), .row25(n32_32_buffer_1_p32), .row26(n32_32_buffer_1_p33),
    .row27(n32_32_buffer_1_p34), .row28(n32_32_buffer_1_p35), .row29(n32_32_buffer_1_p36),
    .row30(n32_32_buffer_1_p37), .row31(n32_32_buffer_1_p38));

  // Other names for the same wires on the sheet: on = Full_On
endmodule

module _32_32_buffer (
  input  [31:0] Input_row,
  input  [7:0] Row_selector,
  input  Write_row,
  input  [4:0] Output_row_selector,
  input  clock,
  output [31:0] Row_0,
  output [31:0] Row_1,
  output [31:0] Row_2,
  output [31:0] Row_3,
  output [31:0] Row_4,
  output [31:0] Row_5,
  output [31:0] Row_6,
  output [31:0] Row_7,
  output [31:0] Row_8,
  output [31:0] Row_9,
  output [31:0] Row_10,
  output [31:0] Row_11,
  output [31:0] Row_12,
  output [31:0] Row_13,
  output [31:0] Row_14,
  output [31:0] Row_15,
  output [31:0] Selected_row_output,
  output [31:0] Row_16,
  output [31:0] Row_17,
  output [31:0] Row_18,
  output [31:0] Row_19,
  output [31:0] Row_20,
  output [31:0] Row_21,
  output [31:0] Row_22,
  output [31:0] Row_23,
  output [31:0] Row_24,
  output [31:0] Row_25,
  output [31:0] Row_26,
  output [31:0] Row_27,
  output [31:0] Row_28,
  output [31:0] Row_29,
  output [31:0] Row_30,
  output [31:0] Row_31
);

  wire demultiplexer_1_out0, demultiplexer_1_out1, demultiplexer_1_out2, demultiplexer_1_out3,
       demultiplexer_1_out4, demultiplexer_1_out5, demultiplexer_1_out6, demultiplexer_1_out7,
       demultiplexer_1_out8, demultiplexer_1_out9, demultiplexer_1_out10, demultiplexer_1_out11,
       demultiplexer_1_out12, demultiplexer_1_out13, demultiplexer_1_out14, demultiplexer_1_out15,
       demultiplexer_1_out16, demultiplexer_1_out17, demultiplexer_1_out18, demultiplexer_1_out19,
       demultiplexer_1_out20, demultiplexer_1_out21, demultiplexer_1_out22, demultiplexer_1_out23,
       demultiplexer_1_out24, demultiplexer_1_out25, demultiplexer_1_out26, demultiplexer_1_out27,
       demultiplexer_1_out28, demultiplexer_1_out29, demultiplexer_1_out30, demultiplexer_1_out31;
  wire [7:0] register_1_q;

  Register #(.trigger("high")) register_1 (
    .D(Row_selector), .en(Write_row), .Q(register_1_q), .clk(clock));  // open: clr
  // Probe on register_1_q[4:0]
  Demultiplexer #(.select(5), .disabled(0), .enable("false")) demultiplexer_1 (
    .out0(demultiplexer_1_out0), .out1(demultiplexer_1_out1), .out2(demultiplexer_1_out2),
    .out3(demultiplexer_1_out3), .out4(demultiplexer_1_out4), .out5(demultiplexer_1_out5),
    .out6(demultiplexer_1_out6), .out7(demultiplexer_1_out7), .out8(demultiplexer_1_out8),
    .out9(demultiplexer_1_out9), .out10(demultiplexer_1_out10), .out11(demultiplexer_1_out11),
    .out12(demultiplexer_1_out12), .out13(demultiplexer_1_out13), .out14(demultiplexer_1_out14),
    .out15(demultiplexer_1_out15), .out16(demultiplexer_1_out16), .out17(demultiplexer_1_out17),
    .out18(demultiplexer_1_out18), .out19(demultiplexer_1_out19), .out20(demultiplexer_1_out20),
    .out21(demultiplexer_1_out21), .out22(demultiplexer_1_out22), .out23(demultiplexer_1_out23),
    .out24(demultiplexer_1_out24), .out25(demultiplexer_1_out25), .out26(demultiplexer_1_out26),
    .out27(demultiplexer_1_out27), .out28(demultiplexer_1_out28), .out29(demultiplexer_1_out29),
    .out30(demultiplexer_1_out30), .out31(demultiplexer_1_out31), .in(Write_row), .sel(register_1_q[4:0]));
  Register #(.width(32)) register_2 (.D(Input_row), .en(demultiplexer_1_out0), .Q(Row_0), .clk(clock));  // open: clr
  Register #(.width(32)) register_3 (.D(Input_row), .en(demultiplexer_1_out1), .Q(Row_1), .clk(clock));  // open: clr
  Register #(.width(32)) register_4 (.D(Input_row), .en(demultiplexer_1_out2), .Q(Row_2), .clk(clock));  // open: clr
  Register #(.width(32)) register_5 (.D(Input_row), .en(demultiplexer_1_out3), .Q(Row_3), .clk(clock));  // open: clr
  Register #(.width(32)) register_6 (.D(Input_row), .en(demultiplexer_1_out4), .Q(Row_4), .clk(clock));  // open: clr
  Register #(.width(32)) register_7 (.D(Input_row), .en(demultiplexer_1_out5), .Q(Row_5), .clk(clock));  // open: clr
  Register #(.width(32)) register_8 (.D(Input_row), .en(demultiplexer_1_out6), .Q(Row_6), .clk(clock));  // open: clr
  Register #(.width(32)) register_9 (.D(Input_row), .en(demultiplexer_1_out7), .Q(Row_7), .clk(clock));  // open: clr
  Register #(.width(32)) register_10 (.D(Input_row), .en(demultiplexer_1_out8), .Q(Row_8), .clk(clock));  // open: clr
  Register #(.width(32)) register_11 (.D(Input_row), .en(demultiplexer_1_out9), .Q(Row_9), .clk(clock));  // open: clr
  Register #(.width(32)) register_12 (.D(Input_row), .en(demultiplexer_1_out10), .Q(Row_10), .clk(clock));  // open: clr
  Register #(.width(32)) register_13 (.D(Input_row), .en(demultiplexer_1_out11), .Q(Row_11), .clk(clock));  // open: clr
  Register #(.width(32)) register_14 (.D(Input_row), .en(demultiplexer_1_out12), .Q(Row_12), .clk(clock));  // open: clr
  Register #(.width(32)) register_15 (.D(Input_row), .en(demultiplexer_1_out13), .Q(Row_13), .clk(clock));  // open: clr
  Register #(.width(32)) register_16 (.D(Input_row), .en(demultiplexer_1_out14), .Q(Row_14), .clk(clock));  // open: clr
  Register #(.width(32)) register_17 (.D(Input_row), .en(demultiplexer_1_out15), .Q(Row_15), .clk(clock));  // open: clr
  Register #(.width(32)) register_18 (.D(Input_row), .en(demultiplexer_1_out16), .Q(Row_16), .clk(clock));  // open: clr
  Register #(.width(32)) register_19 (.D(Input_row), .en(demultiplexer_1_out17), .Q(Row_17), .clk(clock));  // open: clr
  Register #(.width(32)) register_20 (.D(Input_row), .en(demultiplexer_1_out18), .Q(Row_18), .clk(clock));  // open: clr
  Register #(.width(32)) register_21 (.D(Input_row), .en(demultiplexer_1_out19), .Q(Row_19), .clk(clock));  // open: clr
  Register #(.width(32)) register_22 (.D(Input_row), .en(demultiplexer_1_out20), .Q(Row_20), .clk(clock));  // open: clr
  Register #(.width(32)) register_23 (.D(Input_row), .en(demultiplexer_1_out21), .Q(Row_21), .clk(clock));  // open: clr
  Register #(.width(32)) register_24 (.D(Input_row), .en(demultiplexer_1_out22), .Q(Row_22), .clk(clock));  // open: clr
  Register #(.width(32)) register_25 (.D(Input_row), .en(demultiplexer_1_out23), .Q(Row_23), .clk(clock));  // open: clr
  Register #(.width(32)) register_26 (.D(Input_row), .en(demultiplexer_1_out24), .Q(Row_24), .clk(clock));  // open: clr
  Register #(.width(32)) register_27 (.D(Input_row), .en(demultiplexer_1_out25), .Q(Row_25), .clk(clock));  // open: clr
  Register #(.width(32)) register_28 (.D(Input_row), .en(demultiplexer_1_out26), .Q(Row_26), .clk(clock));  // open: clr
  Register #(.width(32)) register_29 (.D(Input_row), .en(demultiplexer_1_out27), .Q(Row_27), .clk(clock));  // open: clr
  Register #(.width(32)) register_30 (.D(Input_row), .en(demultiplexer_1_out28), .Q(Row_28), .clk(clock));  // open: clr
  Register #(.width(32)) register_31 (.D(Input_row), .en(demultiplexer_1_out29), .Q(Row_29), .clk(clock));  // open: clr
  Register #(.width(32)) register_32 (.D(Input_row), .en(demultiplexer_1_out30), .Q(Row_30), .clk(clock));  // open: clr
  Register #(.width(32)) register_33 (.D(Input_row), .en(demultiplexer_1_out31), .Q(Row_31), .clk(clock));  // open: clr
  Multiplexer #(.select(5), .width(32), .enable("false")) multiplexer_1 (
    .in0(Row_0), .in1(Row_1), .in2(Row_2), .in3(Row_3), .in4(Row_4), .in5(Row_5), .in6(Row_6), .in7(Row_7),
    .in8(Row_8), .in9(Row_9), .in10(Row_10), .in11(Row_11), .in12(Row_12), .in13(Row_13), .in14(Row_14),
    .in15(Row_15), .in16(Row_16), .in17(Row_17), .in18(Row_18), .in19(Row_19), .in20(Row_20), .in21(Row_21),
    .in22(Row_22), .in23(Row_23), .in24(Row_24), .in25(Row_25), .in26(Row_26), .in27(Row_27), .in28(Row_28),
    .in29(Row_29), .in30(Row_30), .in31(Row_31), .out(Selected_row_output), .sel(Output_row_selector));
  // Probe on Output_row_selector

  // Other names for the same wires on the sheet: clk = clock
endmodule

module Keyboard_controller (
  input  [6:0] ASCII_code,
  output [4:0] Y,
  output [4:0] X
);

  wire _0x_y, _0x_y_t, minus_x0y, minus_x_y, minus_x_y_t, or_1_out, or_2_out, or_3_out, or_4_out, or_5_out,
       or_6_out, plus_x0y, plus_x_y, plus_x_y_t;

  Comparator #(.width(7)) comparator_1 (.a(ASCII_code), .b(7'b0110111), .eq(minus_x_y_t));  // open: gt, lt
  Comparator #(.width(7)) comparator_2 (.a(ASCII_code), .b(7'b0110100), .eq(minus_x0y));  // open: gt, lt
  Comparator #(.width(7)) comparator_3 (.a(ASCII_code), .b(7'b0110001), .eq(minus_x_y));  // open: gt, lt
  Comparator #(.width(7)) comparator_4 (.a(ASCII_code), .b(7'b0111000), .eq(_0x_y_t));  // open: gt, lt
  Comparator #(.width(7)) comparator_5 (.a(ASCII_code), .b(7'b0110010), .eq(_0x_y));  // open: gt, lt
  Comparator #(.width(7)) comparator_6 (.a(ASCII_code), .b(7'b0111001), .eq(plus_x_y_t));  // open: gt, lt
  Comparator #(.width(7)) comparator_7 (.a(ASCII_code), .b(7'b0110110), .eq(plus_x0y));  // open: gt, lt
  Comparator #(.width(7)) comparator_8 (.a(ASCII_code), .b(7'b0110011), .eq(plus_x_y));  // open: gt, lt
  or or_1 (or_1_out, minus_x_y_t, _0x_y_t, plus_x_y_t);
  or or_2 (or_2_out, or_1_out, or_3_out);
  or or_3 (or_3_out, minus_x_y, _0x_y, plus_x_y);
  or or_4 (or_4_out, minus_x_y_t, minus_x0y, minus_x_y);
  or or_5 (or_5_out, or_4_out, or_6_out);
  or or_6 (or_6_out, plus_x_y_t, plus_x0y, plus_x_y);
  // Probe on Y
  Counter #(.width(5), .max('h1f)) counter_1 (
    .load(or_1_out), .count(or_2_out), .Q(Y), .clk(or_2_out));  // open: D, carry, clr
  // Probe on X
  Counter #(.width(5), .max('h1f)) counter_2 (
    .load(or_4_out), .count(or_5_out), .Q(X), .clk(or_5_out));  // open: D, carry, clr

  // Notes on the sheet:
  //   Y position
  //   X position
endmodule

module _32_bit_row_destructor (
  input  [31:0] Row,
  input  [4:0] Bit_selector,
  output [7:0] Selected_byte,
  output Selected_bit
);

  wire [31:1] shifter_2_out;
  wire [31:8] shifter_1_out;

  Shifter #(.width(32), .shift("lr")) shifter_1 (
    .in(Row), .\dist ({Bit_selector[4:3], 3'b000}), .out({shifter_1_out, Selected_byte}));
  Shifter #(.width(32), .shift("lr")) shifter_2 (
    .in({shifter_1_out, Selected_byte}), .\dist ({2'b00, Bit_selector[2:0]}),
    .out({shifter_2_out, Selected_bit}));
endmodule
